# Fritzing sketch double sloth (saved by Fritzing 0.9.3b)
stripboards: 1

parts:
  IC2 = IC, DIP package, 14 pins [chip_label=TL074]
  U4 = YD-PJ-3566 [package=audio-jack-3.5mm]
  IC3 = IC, DIP package, 14 pins [chip_label=TL074]
  C4 = Ceramic Capacitor top view [part_number=C1 package="100 mil [THT, multilayer]"]
  R14 = Resistor [tolerance=±5% resistance=100k part_number=R1 package=THT]
  R15 = Resistor [tolerance=±5% resistance=1k package=THT]
  R16 = Resistor [tolerance=±5% resistance=4.7M package=THT]
  R17 = Resistor [tolerance=±5% resistance=1M package=THT]
  R18 = Resistor [tolerance=±5% resistance=100k part_number=R2 package=THT]
  R19 = Resistor [tolerance=±5% resistance=1k part_number=R4 package=THT]
  R20 = Resistor [tolerance=±5% resistance=4.7k package=THT]
  R21 = Resistor [tolerance=±5% resistance=100k package=THT]
  U5 = YD-PJ-3566 [package=audio-jack-3.5mm]
  R22 = Resistor [tolerance=±5% resistance=4.7k package=THT]
  R23 = Resistor [tolerance=±5% resistance=100k package=THT]
  R24 = Vertical Resistor [tolerance=±5% resistance=100k package=THT]
  C7 = Ceramic Capacitor top view [part_number=C1 package="100 mil [THT, multilayer]"]
  C8 = Electrolytic Capacitor [capacitance=47µF package="100 mil [THT, electrolytic]"]
  J3 = molex pin header, 5 pins [form=molex]
  J4 = molex pin header, 5 pins [form=molex]
  U6 = YD-PJ-3566 [package=audio-jack-3.5mm]
  R25 = Resistor [tolerance=±5% resistance=4.7k package=THT]
  LED2 = LED - 3mm [color="Red (633nm)" package="3 mm [THT]"]
  R26 = Resistor [tolerance=±5% resistance=470k package=THT]
  C9 = Ceramic Capacitor top view [part_number=C2 package="100 mil [THT, multilayer]"]
  C10 = Ceramic Capacitor top view [part_number=C1 package="100 mil [THT, multilayer]"]
  R27 = Resistor [tolerance=±5% resistance=1M part_number=R1 package=THT]
  R28 = Resistor [tolerance=±5% resistance=4.7M package=THT]
  R29 = Resistor [tolerance=±5% resistance=10M package=THT]
  R30 = Resistor [tolerance=±5% resistance=1M part_number=R2 package=THT]
  R31 = Resistor [tolerance=±5% resistance=1k part_number=R4 package=THT]
  U7 = YD-PJ-3566 [package=audio-jack-3.5mm]
  R32 = Resistor [tolerance=±5% resistance=6.8M package=THT]
  C11 = Ceramic Capacitor top view [part_number=C1 package="100 mil [THT, multilayer]"]
  R33 = Resistor [tolerance=±5% resistance=4.7k package=THT]
  R34 = Resistor [tolerance=±5% resistance=1M package=THT]
  R35 = Vertical Resistor [tolerance=±5% resistance=100k package=THT]
  R36 = Resistor [tolerance=±5% resistance=100k package=THT]
  U8 = YD-PJ-3566 [package=audio-jack-3.5mm]
  R37 = Resistor [tolerance=±5% resistance=4.7k package=THT]
  U9 = YD-PJ-3566 [package=audio-jack-3.5mm]
  C12 = Electrolytic Capacitor [capacitance=47µF package="100 mil [THT, electrolytic]"]
  R38 = Resistor [tolerance=±5% resistance=470k package=THT]
  LED3 = LED - 3mm [color="Red (633nm)" package="3 mm [THT]"]
  R39 = Resistor [tolerance=±5% resistance=4.7k package=THT]
  C3 = Ceramic Capacitor top view [part_number=C2 package="100 mil [THT, multilayer]"]

nets:
  N1: IC2.pin1, IC2.pin14, C4.1, R18.Pin_0, R19.Pin_0, R20.Pin_0, R23.Pin_1, C7.1, C3.1
  N2: IC2.pin2, IC2.pin13, C4.0, R14.Pin_0, R15.Pin_0, R17.Pin_1, R21.Pin_0, C7.0, C3.0
  N3: IC2.pin3, IC2.pin5, IC2.pin10, IC2.pin12, IC3.pin3, IC3.pin5, IC3.pin10, IC3.pin12, J3.pin2, J3.pin3, J3.pin4, J4.pin2, J4.pin3, J4.pin4
  N4: IC2.pin4, IC2.pin11, IC3.pin4, IC3.pin11, J3.pin1, J3.pin5, J4.pin1, J4.pin5
  N5: IC2.pin6, IC2.pin7, IC2.pin8, IC2.pin9, R16.Pin_0, R17.Pin_0, R23.Pin_0, R24.Pin_0, R24.Pin_1, R25.Pin_0, R26.Pin_0
  N6: U4.pin_1, U4.pin_2, U4.pin_4, R19.Pin_1
  N7: U4.pin_3, U4.pin_5, U5.pin_3, U5.pin_5, R22.Pin_1, C8.-, U6.pin_3, U6.pin_5, LED2.anode, U7.pin_3, U7.pin_5, U8.pin_3, U8.pin_5, R37.Pin_1, U9.pin_3, U9.pin_5, C12.-, LED3.anode
  N8: IC3.pin1, IC3.pin14, C9.1, C10.1, R30.Pin_0, R31.Pin_0, C11.1, R33.Pin_0, R36.Pin_1
  N9: IC3.pin2, IC3.pin13, C9.0, C10.0, R27.Pin_0, R28.Pin_0, R32.Pin_1, C11.0, R34.Pin_0
  N10: IC3.pin6, IC3.pin7, IC3.pin8, IC3.pin9, R29.Pin_0, R32.Pin_0, R35.Pin_0, R35.Pin_1, R36.Pin_0, R38.Pin_0, R39.Pin_0
  N11: R14.Pin_1, R18.Pin_1, R21.Pin_1, C8.+
  N12: R15.Pin_1, R16.Pin_1
  N13: R20.Pin_1, U5.pin_1, U5.pin_2, U5.pin_4, R22.Pin_0
  N14: U6.pin_1, U6.pin_4, R26.Pin_1
  N15: R25.Pin_1, LED2.cathode
  N16: R27.Pin_1, R30.Pin_1, R34.Pin_1, C12.+
  N17: R28.Pin_1, R29.Pin_1
  N18: R31.Pin_1, U7.pin_1, U7.pin_2, U7.pin_4
  N19: R33.Pin_1, U8.pin_1, U8.pin_2, U8.pin_4, R37.Pin_0
  N20: U9.pin_1, U9.pin_2, U9.pin_4, R38.Pin_1
  N21: LED3.cathode, R39.Pin_1

custom parts:
  YD-PJ-3566: Stereo audio jack YD-PJ-3566
  Ceramic Capacitor top view: 100 nF multilayer Ceramic Capacitor breadboard set to top view for perfboard use.
  Vertical Resistor: A generic resistor (0.25W)
